// Logisim project Bird.circ as structural Verilog
module Control_Unit (
  input  [3:0] in_1,
  output [8:0] out_2
);

  ROM #(.addrWidth(4), .dataWidth(9)) rom_1 (.addr(in_1), .data(out_2));  // open: sel

  // Other names for the same wires on the sheet: irld = out_2[0]; memld = out_2[1]; mux = out_2[2]; zfld = out_2[3];
  //   regld = out_2[4]; armux = out_2[5]; pcinc = out_2[6]; pcld = out_2[7]; fetch = out_2[8]

  // Notes on the sheet:
  //   Control Unit for Reptile     -      Including LD, ST, JUMP, JZ
  //   contents of rom_1 (hex, n*v repeats v):
  //   141 51 34 22 0 80 0 18
endmodule

module ALU (
  input  [15:0] Din1,
  input  [15:0] Din2,
  input  [3:0] AluOp,
  output [15:0] AluResult,
  output Zero
);

  wire [15:0] adder_1_out, adder_2_out, Bitwise_And_out, Bitwise_Not_out, Bitwise_Or_out, Bitwise_Xor_out,
       subtractor_1_out, subtractor_2_out;

  assign Bitwise_And_out = Din1 & Din2;  // AND_Gate Bitwise_And, 16 bits wide
  assign Bitwise_Or_out = Din1 | Din2;  // OR_Gate Bitwise_Or, 16 bits wide
  assign Bitwise_Xor_out = Din1 ^ Din2;  // XOR_Gate Bitwise_Xor, 16 bits wide
  assign Bitwise_Not_out = ~Din1;  // NOT_Gate Bitwise_Not, 16 bits wide
  Adder #(.width(16)) adder_1 (.a(Din1), .b(Din2), .out(adder_1_out));  // open: cin, cout
  Subtractor #(.width(16)) subtractor_1 (.a(Din1), .b(Din2), .out(subtractor_1_out));  // open: bin, bout
  Adder #(.width(16)) adder_2 (.a(Din1), .b(16'h1), .out(adder_2_out));  // open: cin, cout
  Subtractor #(.width(16)) subtractor_2 (.a(Din1), .b(16'h1), .out(subtractor_2_out));  // open: bin, bout
  Multiplexer #(.select(4), .width(16)) multiplexer_1 (
    .in0(adder_1_out), .in1(subtractor_1_out), .in2(Bitwise_And_out), .in3(Bitwise_Or_out),
    .in4(Bitwise_Xor_out), .in5(Bitwise_Not_out), .in6(Din1), .in7(adder_2_out), .in8(subtractor_2_out),
    .out(AluResult), .sel(AluOp));  // open: in9, in10, in11, in12, in13, in14, in15, en
  nor nor_1 (Zero, AluResult[0], AluResult[1], AluResult[2], AluResult[3], AluResult[4], AluResult[5], AluResult[6], AluResult[7], AluResult[9], AluResult[10], AluResult[11], AluResult[12], AluResult[13], AluResult[14], AluResult[15], AluResult[8]);

  // Notes on the sheet:
  //   Adder
  //   Substractor
  //   Move
endmodule
